# Fritzing sketch Untitled Sketch 2 (saved by Fritzing 1.0.4)
breadboards: 1

parts:
  R1 = Resistor [tolerance=±5% power=0.25W resistance=220 package=THT]
  R2 = Resistor [tolerance=±5% power=0.25W resistance=220 package=THT]
  R3 = Resistor [tolerance=±5% power=0.25W resistance=220 package=THT]
  R4 = Resistor [tolerance=±5% power=0.25W resistance=220 package=THT]
  R5 = Resistor [tolerance=±5% power=0.25W resistance=220 package=THT]
  R6 = Resistor [tolerance=±5% power=0.25W resistance=220 package=THT]
  R7 = Resistor [tolerance=±5% power=0.25W resistance=10K package=THT]
  R8 = Resistor [tolerance=±5% power=0.25W resistance=10K package=THT]
  R9 = Resistor [tolerance=±5% power=0.25W resistance=10K package=THT]
  R10 = Resistor [tolerance=±5% power=0.25W resistance=10K package=THT]
  R11 = Resistor [tolerance=±5% power=0.25W resistance=10K package=THT]
  R12 = Resistor [tolerance=±5% power=0.25W resistance=10K package=THT]
  U2 = SN74HC194 [package=dil16]
  R13 = Resistor [tolerance=±5% power=0.25W resistance=220 package=THT]
  R14 = Resistor [tolerance=±5% power=0.25W resistance=220 package=THT]
  R15 = Resistor [tolerance=±5% power=0.25W resistance=220 package=THT]
  R16 = Resistor [tolerance=±5% power=0.25W resistance=220 package=THT]
  LED1 = LEDs [package=led10mm]
  LED2 = LEDs [package=led10mm]
  LED3 = LEDs [package=led10mm]
  LED4 = LEDs [package=led10mm]
  SW4 = DIP Switch 6 Position [package=dipswitch-06]

nets:
  N1: R1.Pin_0, SW4.11
  N2: R1.Pin_1, R2.Pin_1, R3.Pin_1, R4.Pin_1, R5.Pin_1, R6.Pin_1, U2.Y2, U2.X2, R14.Pin_0, LED1.C, LED2.C, LED3.C, LED4.C
  N3: R2.Pin_0, SW4.12
  N4: R3.Pin_0, SW4.10
  N5: R4.Pin_0, SW4.9
  N6: R5.Pin_0, SW4.8
  N7: R6.Pin_0, SW4.7
  N8: R7.Pin_0, SW4.1
  N9: R7.Pin_1, R8.Pin_1, R9.Pin_1, R10.Pin_1, R11.Pin_1, R12.Pin_0, R12.Pin_1, R14.Pin_1, LED4.A, SW4.6
  N10: R8.Pin_0, U2.GND, U2.X1, R13.Pin_0, SW4.5
  N11: R9.Pin_0, SW4.2
  N12: R10.Pin_0, U2.INH, SW4.4
  N13: R11.Pin_0, U2.Y1, SW4.3
  N14: U2.Y0, R15.Pin_0
  N15: U2.Y, U2.X3
  N16: U2.X, R16.Pin_0
  N17: R15.Pin_1, LED1.A
  N18: R16.Pin_1, LED2.A

custom parts:
  SN74HC194: Dual 4:1 analog mux
